// Logisim project ALU_update.circ as structural Verilog: 1 circuit, main circuit main
module main (
  input  [7:0] A,
  input  [7:0] B,
  input  Cin,
  input  [3:0] Funsel,
  output [7:0] OutALU,
  output [3:0] flags_enable,
  output [3:0] OutFlag__ZCNO
);

  wire main_1_cout, main_1_overflow, main_2_p3, main_2_p10, main_2_p11, main_2_p12, main_2_p13, main_2_p14,
       main_2_p15, multiplexer_3_out, multiplexer_4_out, multiplexer_5_out, multiplexer_7_out;
  wire [7:0] and_1_out, main_1_output, main_2_p4, main_2_p5, main_2_p6, main_2_p7, main_2_p8, main_2_p9,
       not_1_out, not_2_out, or_1_out, xor_1_out;

  assign not_1_out = ~A;  // NOT_Gate not_1, 8 bits wide
  assign and_1_out = A & B;  // AND_Gate and_1, 8 bits wide
  assign or_1_out = A | B;  // OR_Gate or_1, 8 bits wide
  assign xor_1_out = B ^ A;  // XOR_Gate xor_1, 8 bits wide
  assign not_2_out = ~B;  // NOT_Gate not_2, 8 bits wide
  adder_main main_1 (
    .A(A), .B(B), .Funsel_last2(Funsel[1:0]), .Cin(Cin), .Cout(main_1_cout), .Output(main_1_output),
    .Overflow(main_1_overflow));
  // Shifters_main main_2: pin names not known; wires that end beside it: A, Cin, main_2_p3, main_2_p4, main_2_p5, main_2_p6, main_2_p7, main_2_p8, main_2_p9, main_2_p10, main_2_p11, main_2_p12, main_2_p13, main_2_p14, main_2_p15
  Multiplexer #(.enable("false")) multiplexer_1 (
    .in0(main_1_overflow), .in1(multiplexer_3_out), .out(OutFlag__ZCNO[3]), .sel(Funsel[3]));
  Multiplexer #(.enable("false")) multiplexer_2 (
    .in0(main_1_cout), .in1(multiplexer_5_out), .out(OutFlag__ZCNO[1]), .sel(Funsel[3]));
  Multiplexer #(.select(2), .enable("false")) multiplexer_3 (
    .in0(main_2_p3), .in1(1'b0), .in2(main_2_p13), .in3(main_2_p12), .out(multiplexer_3_out),
    .sel(Funsel[1:0]));
  Multiplexer #(.enable("false")) multiplexer_4 (
    .in0(main_2_p14), .in1(main_2_p15), .out(multiplexer_4_out), .sel(Funsel[0]));
  Multiplexer #(.enable("false")) multiplexer_5 (
    .in0(multiplexer_7_out), .in1(multiplexer_4_out), .out(multiplexer_5_out), .sel(Funsel[2]));
  Multiplexer #(.select(4), .width(8), .enable("false")) multiplexer_6 (
    .in0(A), .in1(B), .in2(not_1_out), .in3(not_2_out), .in4(main_1_output), .in5(main_1_output),
    .in6(main_1_output), .in7(and_1_out), .in8(or_1_out), .in9(xor_1_out), .in10(main_2_p4),
    .in11(main_2_p5), .in12(main_2_p6), .in13(main_2_p7), .in14(main_2_p8), .in15(main_2_p9), .out(OutALU),
    .sel(Funsel));
  Multiplexer #(.enable("false")) multiplexer_7 (
    .in0(main_2_p11), .in1(main_2_p10), .out(multiplexer_7_out), .sel(Funsel[0]));
  nor nor_1 (OutFlag__ZCNO[0], OutALU[0], OutALU[1], OutALU[2], OutALU[3], OutALU[4], OutALU[5], OutALU[6], OutALU[7]);
  Multiplexer #(.select(4), .width(4), .enable("false")) multiplexer_8 (
    .in0(4'b0101), .in1(4'b0101), .in2(4'b0101), .in3(4'b0101), .in4(4'b1111), .in5(4'b1111), .in6(4'b1111),
    .in7(4'b0101), .in8(4'b0101), .in9(4'b0101), .in10(4'b0111), .in11(4'b0111), .in12(4'b1101),
    .in13(4'b0001), .in14(4'b1111), .in15(4'b1111), .out(flags_enable), .sel(Funsel));

  assign OutFlag__ZCNO[2] = OutALU[7];
endmodule
