// Logisim project CU (serhat).circ as structural Verilog: 1 circuit, main circuit main
module main (
  input  Z,
  input  [15:0] INSTRUCTION,
  input  rewind,
  input  CLK,
  input  [1:0] OUTASEL,
  input  [1:0] OUTBSEL,
  input  [1:0] OUTCSEL,
  output [1:0] deneme
);

  wire and_1_out, and_2_out, and_3_out, and_4_out, and_5_out, and_6_out, and_7_out, and_8_out, and_9_out,
       and_10_out, and_11_out, and_12_out, and_13_out, and_14_out, and_15_out, and_16_out, and_17_out,
       d_ff_1_q, not_1_out, not_2_out, not_3_out, not_4_out, not_5_out, not_6_out, not_7_out, not_8_out,
       not_9_out, not_10_out, not_11_out, not_12_out, not_13_out, Opcode0, Opcode1, Opcode2, Opcode3,
       Opcode4, Opcode5, Opcode6, Opcode7, Opcode8, Opcode9, Opcode10, Opcode11, Opcode12, Opcode13,
       Opcode14, Opcode15, Opcode16, Opcode17, Opcode18, Opcode19, or_1_out, or_2_out, or_3_out, or_4_out,
       or_5_out, or_6_out, or_7_out, or_8_out, or_9_out, or_10_out, or_11_out, or_12_out, or_13_out,
       or_14_out, or_15_out, or_16_out, or_17_out, T0, T1, T2, T3, T4, T5, T6, T7;
  wire [2:0] counter_1_q;
  wire [3:0] DESTREG_2A_2, DESTREG_2B_2, REGSEL_2A_0, SRCREG1_2A_2, SRCREG1_2B_2, SRCREG2_2A_2, SRCREG2_2B_2;

  Counter #(.width(3), .max('h7)) counter_1 (
    .count(1'b1), .Q(counter_1_q), .clk(CLK), .clr(d_ff_1_q));  // open: load, D, carry
  D_Flip_Flop d_ff_1 (.clk(CLK), .D(rewind), .Q(d_ff_1_q), .en(1'b1), .reset(d_ff_1_q));  // open: Qn, preset
  not not_1 (not_1_out, INSTRUCTION[5]);
  Decoder #(.select(3), .enable("false")) decoder_1 (
    .out0(T0), .out1(T1), .out2(T2), .out3(T3), .out4(T4), .out5(T5), .out6(T6), .out7(T7), .sel(counter_1_q));
  Decoder #(.select(2)) decoder_2 (
    .out0(SRCREG2_2A_2[3]), .out1(SRCREG2_2A_2[1]), .out2(SRCREG2_2A_2[2]), .out3(SRCREG2_2A_2[0]),
    .sel(INSTRUCTION[4:3]), .en(not_1_out));
  Decoder #(.select(2)) decoder_3 (
    .out0(SRCREG2_2B_2[3]), .out1(SRCREG2_2B_2[2]), .out2(SRCREG2_2B_2[1]), .out3(SRCREG2_2B_2[0]),
    .sel(INSTRUCTION[4:3]), .en(INSTRUCTION[5]));
  Decoder #(.select(5), .enable("false")) decoder_4 (
    .out0(Opcode0), .out1(Opcode1), .out2(Opcode2), .out3(Opcode3), .out4(Opcode4), .out5(Opcode5),
    .out6(Opcode6), .out7(Opcode7), .out8(Opcode8), .out9(Opcode9), .out10(Opcode10), .out11(Opcode11),
    .out12(Opcode12), .out13(Opcode13), .out14(Opcode14), .out15(Opcode15), .out16(Opcode16),
    .out17(Opcode17), .out18(Opcode18), .out19(Opcode19), .sel(INSTRUCTION[15:11]));  // open: out20, out21, out22, out23, out24, out25, out26, out27, out28, out29, out30, out31
  Decoder #(.select(2), .enable("false")) decoder_5 (
    .out0(REGSEL_2A_0[0]), .out1(REGSEL_2A_0[1]), .out2(REGSEL_2A_0[2]), .out3(REGSEL_2A_0[3]),
    .sel(INSTRUCTION[10:9]));
  not not_2 (not_2_out, INSTRUCTION[10]);
  not not_3 (not_3_out, INSTRUCTION[2]);
  Decoder #(.select(2)) decoder_6 (
    .out0(DESTREG_2A_2[3]), .out1(DESTREG_2A_2[1]), .out2(DESTREG_2A_2[2]), .out3(DESTREG_2A_2[0]),
    .sel(INSTRUCTION[9:8]), .en(not_2_out));
  Decoder #(.select(2)) decoder_7 (
    .out0(DESTREG_2B_2[3]), .out1(DESTREG_2B_2[2]), .out2(DESTREG_2B_2[1]), .out3(DESTREG_2B_2[0]),
    .sel(INSTRUCTION[9:8]), .en(INSTRUCTION[10]));
  Decoder #(.select(2)) decoder_8 (
    .out0(SRCREG1_2A_2[3]), .out1(SRCREG1_2A_2[1]), .out2(SRCREG1_2A_2[2]), .out3(SRCREG1_2A_2[0]),
    .sel(INSTRUCTION[1:0]), .en(not_3_out));
  Decoder #(.select(2)) decoder_9 (
    .out0(SRCREG1_2B_2[3]), .out1(SRCREG1_2B_2[2]), .out2(SRCREG1_2B_2[1]), .out3(SRCREG1_2B_2[0]),
    .sel(INSTRUCTION[1:0]), .en(INSTRUCTION[2]));
  not not_4 (not_4_out, INSTRUCTION[5]);
  and and_1 (and_1_out, T4, Opcode0);
  and and_2 (and_2_out, T4, Opcode4);
  and and_3 (and_3_out, T3, Opcode14);
  and and_4 (and_4_out, T3, INSTRUCTION[5], Opcode2);
  buf or_1 (or_1_out, and_4_out);  // OR_Gate
  and and_5 (and_5_out, T3, not_4_out, Opcode2);
  or or_2 (or_2_out, and_1_out, and_2_out);
  buf or_3 (or_3_out, and_3_out);  // OR_Gate
  assign deneme = or_3_out ? 2'b00 : 2'bz;  // Controlled_Buffer controlled_buffer_1
  assign deneme = or_1_out ? 2'b10 : 2'bz;  // Controlled_Buffer controlled_buffer_2
  buf or_4 (or_4_out, and_5_out);  // OR_Gate
  assign deneme = or_2_out ? 2'b01 : 2'bz;  // Controlled_Buffer controlled_buffer_3
  assign deneme = or_4_out ? 2'b11 : 2'bz;  // Controlled_Buffer controlled_buffer_4
  not not_5 (not_5_out, INSTRUCTION[5]);
  or or_5 (or_5_out, Opcode5, Opcode9, Opcode10, Opcode12, Opcode13);
  or or_6 (or_6_out, Opcode0, Opcode1);
  not not_6 (not_6_out, INSTRUCTION[0]);
  and and_6 (and_6_out, T5, or_6_out);
  and and_7 (and_7_out, T4, not_5_out, or_5_out);
  and and_8 (and_8_out, T4, not_6_out, Opcode11);
  and and_9 (and_9_out, T4, INSTRUCTION[5], Opcode6);
  or or_7 (or_7_out, and_7_out, and_8_out);
  assign OUTASEL = or_7_out ? SRCREG1_2A_2[1:0] : 2'bz;  // Controlled_Buffer controlled_buffer_5
  assign OUTASEL = and_9_out ? SRCREG2_2A_2[1:0] : 2'bz;  // Controlled_Buffer controlled_buffer_6
  assign OUTASEL = and_6_out ? INSTRUCTION[10:9] : 2'bz;  // Controlled_Buffer controlled_buffer_7
  not not_7 (not_7_out, INSTRUCTION[5]);
  not not_8 (not_8_out, INSTRUCTION[2]);
  or or_8 (or_8_out, Opcode5, Opcode9, Opcode10);
  not not_9 (not_9_out, INSTRUCTION[2]);
  or or_9 (or_9_out, Opcode9, Opcode10);
  not not_10 (not_10_out, INSTRUCTION[5]);
  or or_10 (or_10_out, Opcode2, Opcode6, Opcode7, Opcode8);
  not not_11 (not_11_out, INSTRUCTION[5]);
  or or_11 (or_11_out, Opcode5, Opcode9, Opcode10);
  and and_10 (and_10_out, T4, not_7_out, not_8_out, or_8_out);
  and and_11 (and_11_out, T4, INSTRUCTION[5], not_9_out, or_9_out);
  and and_12 (and_12_out, T4, not_10_out, or_10_out);
  and and_13 (and_13_out, T4, INSTRUCTION[2], or_11_out);
  or or_12 (or_12_out, and_10_out, and_11_out);
  or or_13 (or_13_out, and_12_out, and_13_out);
  assign OUTBSEL = or_13_out ? SRCREG1_2A_2[1:0] : 2'bz;  // Controlled_Buffer controlled_buffer_8
  assign OUTBSEL = or_12_out ? SRCREG2_2A_2[1:0] : 2'bz;  // Controlled_Buffer controlled_buffer_9
  not not_12 (not_12_out, INSTRUCTION[0]);
  or or_14 (or_14_out, Opcode9, Opcode10);
  not not_13 (not_13_out, INSTRUCTION[5]);
  or or_15 (or_15_out, Opcode6, Opcode9, Opcode10);
  or or_16 (or_16_out, Opcode2, Opcode7, Opcode8, Opcode11, Opcode12, Opcode13);
  and and_14 (and_14_out, T4, not_13_out, INSTRUCTION[0], or_15_out);
  and and_15 (and_15_out, T4, INSTRUCTION[5], or_16_out);
  and and_16 (and_16_out, T4, INSTRUCTION[5], not_12_out, or_14_out);
  and and_17 (and_17_out, T4, Opcode17);
  or or_17 (or_17_out, and_15_out, and_16_out);
  assign OUTCSEL = and_14_out ? SRCREG2_2B_2[1:0] : 2'bz;  // Controlled_Buffer controlled_buffer_10
  assign OUTCSEL = and_17_out ? 2'b00 : 2'bz;  // Controlled_Buffer controlled_buffer_11
  assign OUTCSEL = or_17_out ? SRCREG1_2B_2[1:0] : 2'bz;  // Controlled_Buffer controlled_buffer_12

  // Other names for the same wires on the sheet: IR11 = INSTRUCTION[11]; IR12 = INSTRUCTION[12];
  //   IR13 = INSTRUCTION[13]; IR14 = INSTRUCTION[14]; IR15 = INSTRUCTION[15]; IR3 = INSTRUCTION[3];
  //   IR4 = INSTRUCTION[4]; IR0 = INSTRUCTION[0]; IR1 = INSTRUCTION[1]; IR8 = INSTRUCTION[8]; IR9 = INSTRUCTION[9];
  //   IR10 = INSTRUCTION[10]; IR2 = INSTRUCTION[2]; IR5 = INSTRUCTION[5]; IR6 = INSTRUCTION[6]; IR7 = INSTRUCTION[7]

  // Notes on the sheet:
  //   Opcode
  //   MUXASEL
  //   OUTASEL
  //   OUTBSEL
  //   OUTCSEL
endmodule
