// Logisim project CU.circ as structural Verilog: 1 circuit, main circuit main
module main (
  input  [15:0] INSTRUCTION,
  input  CLK
);

  wire d_ff_1_q, decoder_5_out0, decoder_5_out1, not_1_out, Opcode0, Opcode1, Opcode2, Opcode3, Opcode4,
       Opcode5, Opcode6, Opcode7, Opcode8, Opcode9, Opcode10, Opcode11, Opcode12, Opcode13, Opcode14,
       Opcode15, Opcode16, Opcode17, Opcode18, Opcode19, Rewind, T0, T1, T2, T3, T4, T5, T6, T7;
  wire [2:0] counter_1_q, DESTREG_2B_2;
  wire [3:0] DESTREG_2A_2, REGSEL_2A_0;

  Counter #(.width(3), .max('h7)) counter_1 (
    .count(1'b1), .Q(counter_1_q), .clk(CLK), .clr(d_ff_1_q));  // open: load, D, carry
  D_Flip_Flop d_ff_1 (.clk(CLK), .D(Rewind), .Q(d_ff_1_q), .en(1'b1), .reset(d_ff_1_q));  // open: Qn, preset
  Decoder #(.select(3), .enable("false")) decoder_1 (
    .out0(T0), .out1(T1), .out2(T2), .out3(T3), .out4(T4), .out5(T5), .out6(T6), .out7(T7), .sel(counter_1_q));
  Decoder #(.select(5), .enable("false")) decoder_2 (
    .out0(Opcode0), .out1(Opcode1), .out2(Opcode2), .out3(Opcode3), .out4(Opcode4), .out5(Opcode5),
    .out6(Opcode6), .out7(Opcode7), .out8(Opcode8), .out9(Opcode9), .out10(Opcode10), .out11(Opcode11),
    .out12(Opcode12), .out13(Opcode13), .out14(Opcode14), .out15(Opcode15), .out16(Opcode16),
    .out17(Opcode17), .out18(Opcode18), .out19(Opcode19), .sel(INSTRUCTION[15:11]));  // open: out20, out21, out22, out23, out24, out25, out26, out27, out28, out29, out30, out31
  Decoder #(.select(2), .enable("false")) decoder_3 (
    .out0(REGSEL_2A_0[0]), .out1(REGSEL_2A_0[1]), .out2(REGSEL_2A_0[2]), .out3(REGSEL_2A_0[3]),
    .sel(INSTRUCTION[10:9]));
  not not_1 (not_1_out, INSTRUCTION[10]);
  Decoder #(.select(2)) decoder_4 (
    .out0(DESTREG_2A_2[3]), .out1(DESTREG_2A_2[1]), .out2(DESTREG_2A_2[2]), .out3(DESTREG_2A_2[0]),
    .sel(INSTRUCTION[9:8]), .en(not_1_out));
  Decoder #(.select(2)) decoder_5 (
    .out0(decoder_5_out0), .out1(decoder_5_out1), .out2(DESTREG_2B_2[1]), .out3(DESTREG_2B_2[2]),
    .sel(INSTRUCTION[9:8]), .en(INSTRUCTION[10]));
  or or_1 (DESTREG_2B_2[0], decoder_5_out0, decoder_5_out1);

  // Other names for the same wires on the sheet: IR11 = INSTRUCTION[11]; IR12 = INSTRUCTION[12];
  //   IR13 = INSTRUCTION[13]; IR14 = INSTRUCTION[14]; IR15 = INSTRUCTION[15]; IR8 = INSTRUCTION[8];
  //   IR9 = INSTRUCTION[9]; IR0 = INSTRUCTION[0]; IR1 = INSTRUCTION[1]; IR2 = INSTRUCTION[2]; IR3 = INSTRUCTION[3];
  //   IR4 = INSTRUCTION[4]; IR5 = INSTRUCTION[5]; IR6 = INSTRUCTION[6]; IR7 = INSTRUCTION[7]; IR10 = INSTRUCTION[10]

  // Notes on the sheet:
  //   Opcode
endmodule
