// Logisim project CircularShift.circ as structural Verilog: 1 circuit, main circuit main
module main (
  input  C,
  input  [7:0] IN,
  output CSR_OVERFLOW,
  output CSL_OVERFLOW,
  output [7:0] CSL,
  output CSL_CARRY,
  output CSR_CARRY,
  output [7:0] CSR
);

  xor xor_1 (CSR_OVERFLOW, IN[0], IN[7]);
  xor xor_2 (CSL_OVERFLOW, IN[6], IN[7]);

  assign CSL = {IN[6:0], C};
  assign CSL_CARRY = IN[7];
  assign CSR = {C, IN[7:1]};
  assign CSR_CARRY = IN[0];
endmodule
