// Logisim project LogicalShift.circ as structural Verilog: 1 circuit, main circuit main
module main (
  input  [7:0] IN,
  output LSR_CARRY,
  output LSL_CARRY,
  output [7:0] LSL,
  output [7:0] LSR
);

  Shifter shifter_1 (.in(IN), .\dist (3'b001), .out(LSL));
  Shifter #(.shift("lr")) shifter_2 (.in(IN), .\dist (3'b001), .out(LSR));

  assign LSL_CARRY = IN[7];
  assign LSR_CARRY = IN[0];
endmodule
