// Logisim project PART 2A.circ as structural Verilog: 1 circuit, main circuit main
module main (
  input  clk,
  input  [7:0] I,
  input  [1:0] OutASel,
  input  [1:0] OutBSel,
  input  [1:0] FunSel,
  input  [3:0] RegSel,
  output [7:0] OutA,
  output [7:0] OutB
);

  wire [7:0] R0_q, R1_q, R2_q, R3_q;

  REGISTER___8_BIT_main R0 (.I(I), .CLK(clk), .FunSel(FunSel), .E(RegSel[0]), .Q(R0_q));
  REGISTER___8_BIT_main R1 (.I(I), .CLK(clk), .FunSel(FunSel), .E(RegSel[1]), .Q(R1_q));
  REGISTER___8_BIT_main R2 (.I(I), .CLK(clk), .FunSel(FunSel), .E(RegSel[2]), .Q(R2_q));
  REGISTER___8_BIT_main R3 (.I(I), .CLK(clk), .FunSel(FunSel), .E(RegSel[3]), .Q(R3_q));
  Multiplexer #(.select(2), .width(8)) multiplexer_1 (
    .in0(R0_q), .in1(R1_q), .in2(R2_q), .in3(R3_q), .out(OutB), .sel(OutBSel), .en(1'b1));
  Multiplexer #(.select(2), .width(8)) multiplexer_2 (
    .in0(R0_q), .in1(R1_q), .in2(R2_q), .in3(R3_q), .out(OutA), .sel(OutASel), .en(1'b1));
endmodule
