// Logisim project PART 2B.circ as structural Verilog: 1 circuit, main circuit main
module main (
  input  CLK,
  input  [7:0] I,
  input  [1:0] OutCSel,
  input  [1:0] OutDSel,
  input  [1:0] FunSel,
  input  [2:0] RegSel,
  output [7:0] OutC,
  output [7:0] OutD
);

  wire [7:0] AR_q, PC_q, SP_q;

  Multiplexer #(.select(2), .width(8)) multiplexer_1 (
    .in0(PC_q), .in1(AR_q), .in2(SP_q), .in3(PC_q), .out(OutC), .sel(OutCSel), .en(1'b1));
  REGISTER___8_BIT_main PC (.I(I), .CLK(CLK), .FunSel(FunSel), .E(RegSel[0]), .Q(PC_q));
  REGISTER___8_BIT_main AR (.I(I), .CLK(CLK), .FunSel(FunSel), .E(RegSel[1]), .Q(AR_q));
  REGISTER___8_BIT_main SP (.I(I), .CLK(CLK), .FunSel(FunSel), .E(RegSel[2]), .Q(SP_q));
  Multiplexer #(.select(2), .width(8)) multiplexer_2 (
    .in0(PC_q), .in1(AR_q), .in2(SP_q), .in3(PC_q), .out(OutD), .sel(OutDSel), .en(1'b1));
endmodule
