// Logisim project PART 2C.circ as structural Verilog: 1 circuit, main circuit main
module main (
  input  CLK,
  input  EN,
  input  [1:0] Funsel,
  input  [7:0] IN_0_7,
  input  L_H,
  output [15:0] OUT
);

  wire and_1_out, and_2_out, not_1_out;
  wire [7:0] _8bit_D_FF_2_out, _8bit_D_FF_out, demultiplexer_1_out0, demultiplexer_1_out1, multiplexer_2_out,
       multiplexer_3_out;
  wire [15:0] adder_1_out, multiplexer_1_out, subtractor_1_out;

  Subtractor #(.width(16)) subtractor_1 (.a(16'h1), .b(OUT), .out(subtractor_1_out));  // open: bin, bout
  Multiplexer #(.select(2), .width(16)) multiplexer_1 (
    .in0({16{1'b0}}), .in1(adder_1_out), .in2(subtractor_1_out),
    .in3({multiplexer_3_out, multiplexer_2_out}), .out(multiplexer_1_out), .sel(Funsel), .en(EN));
  Adder #(.width(16)) adder_1 (.a(OUT), .b(16'h1), .out(adder_1_out));  // open: cin, cout
  Demultiplexer #(.width(8), .enable("false")) demultiplexer_1 (
    .out0(demultiplexer_1_out0), .out1(demultiplexer_1_out1), .in(IN_0_7), .sel(L_H));
  _16bit_D_Latch_main _16_Bit_D_FF (.IN(multiplexer_1_out), .CLR(1'b0), .EN(EN), .CLK(CLK), .OUT(OUT));
  not not_1 (not_1_out, L_H);
  and and_1 (and_1_out, EN, not_1_out);
  and and_2 (and_2_out, EN, L_H);
  _8bit_D_Latch_main _8bit_D_FF (
    .IN(demultiplexer_1_out0), .CLR(1'b0), .EN(and_1_out), .CLK(CLK), .OUT(_8bit_D_FF_out));
  Multiplexer #(.width(8)) multiplexer_2 (
    .in0(demultiplexer_1_out0), .in1(_8bit_D_FF_out), .out(multiplexer_2_out), .sel(L_H), .en(EN));
  _8bit_D_Latch_main _8bit_D_FF_2 (
    .IN(demultiplexer_1_out1), .CLR(1'b0), .EN(and_2_out), .CLK(CLK), .OUT(_8bit_D_FF_2_out));
  Multiplexer #(.width(8)) multiplexer_3 (
    .in0(_8bit_D_FF_2_out), .in1(demultiplexer_1_out1), .out(multiplexer_3_out), .sel(L_H), .en(EN));

  // Notes on the sheet:
  //   CLR
  //   ADD-SUB
endmodule
