// Logisim project Project3.circ as structural Verilog: 1 circuit, main circuit main
module main (
  input  [7:0] IR_8_15
);

  wire CLK, Enable_2A, Enable_2B, Enable_2C, Enable_MuxA, Enable_MuxB, Enable_MuxC, EnableRAM, L_H, Load,
       MuxCSel, Read, Z;
  wire [1:0] FunSel_2A, FunSel_2B, FunSel_2C, MuxASel, MuxBSel, OuBSel, OutASel, OutBSel, OutCSel, OutDSel;
  wire [2:0] RegSel_2B;
  wire [3:0] FunSel_ALU, RegSel_2A;
  wire [3:1] main_3_outflag__zcno;
  wire [7:0] IR, main_2_outa, main_2_outb, main_3_outalu, main_4_outc, main_4_outd, multiplexer_1_out,
       multiplexer_2_out, multiplexer_3_out, ram_1_data;

  Clock clock_1 (.out(CLK));
  Multiplexer #(.select(2), .width(8)) multiplexer_1 (
    .in0(IR), .in1(ram_1_data), .in2(main_4_outc), .in3(main_3_outalu), .out(multiplexer_1_out),
    .sel(MuxASel), .en(Enable_MuxA));
  PART_2C_main main_1 (.CLK(CLK), .EN(Enable_2C), .Funsel(FunSel_2C), .IN(ram_1_data), .L_H(L_H), .OUT({IR_8_15, IR}));
  PART_2A_main main_2 (
    .I(multiplexer_1_out), .OutA(main_2_outa), .OutB(main_2_outb), .clk(CLK), .OutASel(OutASel),
    .OutBSel(OuBSel), .FunSel(FunSel_2A), .EN(Enable_2A), .RegSel(RegSel_2A));
  Multiplexer #(.width(8)) multiplexer_2 (
    .in0(multiplexer_1_out), .in1(main_2_outa), .out(multiplexer_2_out), .sel(MuxCSel), .en(Enable_MuxC));
  Multiplexer #(.select(2), .width(8)) multiplexer_3 (
    .in1(IR), .in2(ram_1_data), .in3(main_3_outalu), .out(multiplexer_3_out), .sel(MuxBSel), .en(Enable_MuxB));  // open: in0
  Part1_main main_3 (
    .A(multiplexer_2_out), .B(main_2_outb), .FunSel(FunSel_ALU), .OutALU(main_3_outalu),
    .OutFlag__ZCNO({main_3_outflag__zcno, Z}));  // open: CLK
  PART_2B_main main_4 (
    .I(multiplexer_3_out), .OutC(main_4_outc), .OutD(main_4_outd), .CLK(CLK), .OutCSel(OutCSel),
    .OutDSel(OutDSel), .FunSel(FunSel_2B), .EN(Enable_2B), .RegSel(RegSel_2B));
  RAM #(.bus("separate")) ram_1 (
    .addr(main_4_outd), .din(main_3_outalu), .data(ram_1_data), .str(Load), .sel(EnableRAM), .ld(Read));  // open: clk, clr
  CU_updated_main main_5 (
    .Z(Z), .INSTRUCTION({IR_8_15, IR}), .CLK(CLK), .Enable_2C(Enable_2C), .OutDSel(OutDSel), .L_H(L_H),
    .FunSel_2C(FunSel_2C), .RegSel_2A(RegSel_2A), .RegSel_2B(RegSel_2B), .EnableRam(EnableRAM), .Read(Read),
    .Load(Load), .OUTASEL(OutASel), .OUTBSEL(OutBSel), .OUTCSEL(OutCSel), .MuxASelEnable(Enable_MuxA),
    .MuxASel(MuxASel), .MuxBSelEnable(Enable_MuxB), .MuxBSel(MuxBSel), .MuxCSelEnable(Enable_MuxC),
    .MuxCSel(MuxCSel), .Enable_2A(Enable_2A), .Enable_2B(Enable_2B), .FunSel2A(FunSel_2A),
    .FunSel2B(FunSel_2B), .FunSel_ALU(FunSel_ALU));

  // Other names for the same wires on the sheet: IR[15:8] = IR_8_15
endmodule
