// Logisim project Shifters.circ as structural Verilog: 1 circuit, main circuit main
module main (
  input  [7:0] IN,
  input  C,
  output CARRY,
  output OVFLW,
  output [7:0] LSL,
  output [7:0] LSR,
  output [7:0] ASL,
  output [7:0] ASR,
  output [7:0] CSL,
  output [7:0] CSR,
  output LSR_CARRY,
  output LSL_CARRY,
  output CSR_OFLW,
  output CSL_OVFLW,
  output CSL_CARRY,
  output CSR_CARRY
);

  LogicalShift_main main_1 (.IN(IN), .LSR_CARRY(LSR_CARRY), .LSL_CARRY(LSL_CARRY), .LSL(LSL), .LSR(LSR));
  ArithmeticShift_main main_2 (.IN(IN), .ASL(ASL), .ASR(ASR));
  CircularShift_main main_3 (
    .C(C), .IN(IN), .CSR_OVERFLOW(CSR_OFLW), .CSL_OVERFLOW(CSL_OVFLW), .CSL(CSL), .CSL_CARRY(CSL_CARRY),
    .CSR_CARRY(CSR_CARRY), .CSR(CSR));

  assign CARRY = 1'b0;
  assign OVFLW = 1'b0;
endmodule
