// Logisim project adder.circ as structural Verilog: 1 circuit, main circuit main
module main (
  input  Cin,
  input  [7:0] A,
  input  [7:0] B,
  input  [1:0] Funsel_last2,
  output [7:0] Output,
  output Cout,
  output Overflow
);

  wire adder_1_cout, multiplexer_2_out, multiplexer_3_out, not_2_out;
  wire [7:0] adder_1_out, multiplexer_1_out, not_1_out;

  assign not_1_out = ~B;  // NOT_Gate not_1, 8 bits wide
  Multiplexer #(.select(2), .width(8)) multiplexer_1 (
    .in0(B), .in1(B), .in2(not_1_out), .in3(B), .out(multiplexer_1_out), .sel(Funsel_last2), .en(1'b1));
  Multiplexer #(.select(2)) multiplexer_2 (
    .in0(Cout), .in1(Cout), .in2(not_2_out), .in3(Cout), .out(multiplexer_2_out), .sel(Funsel_last2),
    .en(1'b1));
  Adder adder_1 (.a(A), .b(multiplexer_1_out), .out(adder_1_out), .cin(multiplexer_3_out), .cout(adder_1_cout));
  and and_1 (Cout, adder_1_cout, 1'b1);
  not not_2 (not_2_out, Cout);
  and and_2 (Overflow, 1'b1, multiplexer_2_out);
  Multiplexer #(.select(2)) multiplexer_3 (
    .in0(1'b0), .in1(Cin), .in2(1'b1), .in3(1'b0), .out(multiplexer_3_out), .sel(Funsel_last2), .en(1'b1));
  Multiplexer #(.width(8)) multiplexer_4 (.in0({8{1'b0}}), .in1(adder_1_out), .out(Output), .sel(1'b1), .en(1'b1));
endmodule
