// Logisim project microop decoder.circ as structural Verilog: 1 circuit, main circuit main
module main (
  input  [5:0] MicroOp
);

  wire OP0, OP1, OP2, OP3, OP4, OP5, OP6, OP7, OP8, OP9, OP10, OP11, OP12, OP13, OP14, OP15, OP16, OP17,
       OP18, OP19, OP20, OP21, OP22, OP23, OP24, OP25, OP26, OP27, OP28, OP29, OP30, OP31, OP32, OP33, OP34,
       OP35, OP36, OP37, OP38, OP39, OP40, OP41, OP42, OP43, OP44, OP45, OP46, OP47, OP48, OP49, OP50, OP51,
       OP52, OP53, OP54, OP55, OP56, OP57, OP58, OP59, OP60, OP61, OP62, OP63, or_1_out, or_2_out, or_3_out;
  wire [1:0] controlled_buffer_1_out, controlled_buffer_3_out;

  DECODER_6_64_main main_1 (
    .INPUT(MicroOp), ._0(OP0), ._1(OP1), ._2(OP2), ._3(OP3), ._4(OP4), ._5(OP5), ._6(OP6), ._7(OP7),
    ._8(OP8), ._9(OP9), ._10(OP10), ._11(OP11), ._12(OP12), ._13(OP13), ._14(OP14), ._15(OP15), ._16(OP16),
    ._17(OP17), ._18(OP18), ._19(OP19), ._20(OP20), ._21(OP21), ._22(OP22), ._23(OP23), ._24(OP24),
    ._25(OP25), ._26(OP26), ._27(OP27), ._28(OP28), ._29(OP29), ._30(OP30), ._31(OP31), ._32(OP32),
    ._33(OP33), ._34(OP34), ._35(OP35), ._36(OP36), ._37(OP37), ._38(OP38), ._39(OP39), ._40(OP40),
    ._41(OP41), ._42(OP42), ._43(OP43), ._44(OP44), ._45(OP45), ._46(OP46), ._47(OP47), ._48(OP48),
    ._49(OP49), ._50(OP50), ._51(OP51), ._52(OP52), ._53(OP53), ._54(OP54), ._55(OP55), ._56(OP56),
    ._57(OP57), ._58(OP58), ._59(OP59), ._60(OP60), ._61(OP61), ._62(OP62), ._63(OP63));
  or or_1 (or_1_out, OP1, OP8);
  assign controlled_buffer_1_out = or_1_out ? 2'b01 : 2'bz;  // Controlled_Buffer controlled_buffer_1
  or or_2 (or_2_out, OP4, OP3, OP5, OP52);
  assign controlled_buffer_1_out = or_2_out ? 2'b11 : 2'bz;  // Controlled_Buffer controlled_buffer_2
  or or_3 (or_3_out, OP6, OP11, OP52);
  assign controlled_buffer_3_out = or_3_out ? 2'b11 : 2'bz;  // Controlled_Buffer controlled_buffer_3
  assign controlled_buffer_1_out = OP0 ? 2'b00 : 2'bz;  // Controlled_Buffer controlled_buffer_4

  // Notes on the sheet:
  //   MUXASEL
endmodule
