// Logisim project project4.circ as structural Verilog: 1 circuit, main circuit main
module main (
  output [7:0] IR_8_15
);

  wire CLK, Enable_2A, Enable_2B, Enable_2C, Enable_MuxA, Enable_MuxB, Enable_MuxC, EnableRAM, L_H, Load,
       MuxCSel, Read, Z;
  wire [1:0] FunSel_2A, FunSel_2B, FunSel_2C, MuxASel, MuxBSel, OutASel, OutBSel, OutCSel, OutDSel;
  wire [2:0] main_3_outflag__zcno, RegSel_2B;
  wire [3:0] FunSel_ALU, RegSel_2A;
  wire [7:0] IR, main_2_outa, main_2_outb, main_3_outalu, main_4_outc, main_4_outd, multiplexer_1_out,
       multiplexer_2_out, multiplexer_3_out, ram_1_data;

  Clock clock_1 (.out(CLK));
  Multiplexer #(.select(2), .width(8)) multiplexer_1 (
    .in0(IR), .in1(ram_1_data), .in2(main_4_outc), .in3(main_3_outalu), .out(multiplexer_1_out),
    .sel(MuxASel), .en(Enable_MuxA));
  PART_2C_main main_1 (.CLK(CLK), .EN(Enable_2C), .Funsel(FunSel_2C), .IN(ram_1_data), .L_H(L_H), .OUT({IR_8_15, IR}));
  PART_2A_main main_2 (
    .I(multiplexer_1_out), .OutA(main_2_outa), .OutB(main_2_outb), .clk(CLK), .OutASel(OutASel),
    .OutBSel(OutBSel), .FunSel(FunSel_2A), .EN(Enable_2A), .RegSel(RegSel_2A));
  Hex_Digit_Display hex_digit_display_1 (.value(IR_8_15[7:4]));  // open: dp
  Multiplexer #(.width(8)) multiplexer_2 (
    .in0(main_4_outc), .in1(main_2_outa), .out(multiplexer_2_out), .sel(MuxCSel), .en(Enable_MuxC));
  Multiplexer #(.select(2), .width(8)) multiplexer_3 (
    .in1(IR), .in2(ram_1_data), .in3(main_3_outalu), .out(multiplexer_3_out), .sel(MuxBSel), .en(Enable_MuxB));  // open: in0
  Hex_Digit_Display hex_digit_display_2 (.value(IR_8_15[3:0]));  // open: dp
  Part1_main main_3 (
    .A(multiplexer_2_out), .B(main_2_outb), .FunSel(FunSel_ALU), .CLK(CLK), .OutALU(main_3_outalu),
    .OutFlag__ZCNO({Z, main_3_outflag__zcno}));
  PART_2B_main main_4 (
    .I(multiplexer_3_out), .OutC(main_4_outc), .OutD(main_4_outd), .CLK(CLK), .OutCSel(OutCSel),
    .OutDSel(OutDSel), .FunSel(FunSel_2B), .EN(Enable_2B), .RegSel(RegSel_2B));
  RAM #(.bus("separate")) ram_1 (
    .addr(main_4_outd), .din(main_3_outalu), .data(ram_1_data), .str(Load), .sel(EnableRAM), .clk(CLK),
    .ld(Read));  // open: clr
  ROM #(.addrWidth(6)) rom_1 ();  // open: addr, data, sel
  ROM rom_2 ();  // open: addr, data, sel

  // Other names for the same wires on the sheet: IR[15:8] = IR_8_15

  // Notes on the sheet:
  //   contents of rom_2 (hex, n*v repeats v):
  //   1 0 3 0 32
endmodule
