// Logisim project sequencer.circ as structural Verilog: 1 circuit, main circuit main
module main (
  input  CLK,
  input  [9:0] MAP,
  input  Z,
  output [5:0] MicroOp
);

  wire and_1_out, and_2_out, and_3_out, multiplexer_2_out, not_1_out, not_2_out, not_3_out;
  wire [1:0] or_1_out;
  wire [9:0] adder_1_out, main_1_output, main_2_output, multiplexer_1_out, rom_1_data;
  wire [13:11] rom_1_data_2;

  not not_1 (not_1_out, or_1_out[0]);
  Adder #(.width(10)) adder_1 (.a(main_2_output), .b(10'h1), .out(adder_1_out));  // open: cin, cout
  _9_BIT_D_FLIP_FLOP_main main_1 (.CLK(CLK), .EN(and_3_out), .INPUT(adder_1_out), .OUTPUT(main_1_output));
  and and_1 (and_1_out, rom_1_data_2[11], or_1_out[0]);
  and and_2 (and_2_out, not_1_out, multiplexer_2_out);
  Multiplexer #(.select(2), .width(10)) multiplexer_1 (
    .in0(adder_1_out), .in1(rom_1_data), .in2(main_1_output), .in3(MAP), .out(multiplexer_1_out),
    .sel(or_1_out));  // open: en
  or or_1 (or_1_out[1], and_1_out, and_2_out);
  not not_2 (not_2_out, Z);
  not not_3 (not_3_out, or_1_out[0]);
  and and_3 (and_3_out, rom_1_data_2[11], not_3_out, multiplexer_2_out);
  Multiplexer #(.select(2), .enable("false")) multiplexer_2 (
    .in0(1'b1), .in1(Z), .in2(not_2_out), .out(multiplexer_2_out), .sel(rom_1_data_2[13:12]));  // open: in3
  _9_BIT_D_FLIP_FLOP_main main_2 (.CLK(CLK), .INPUT(multiplexer_1_out), .OUTPUT(main_2_output));  // open: EN
  ROM #(.addrWidth(10), .dataWidth(20)) rom_1 (
    .addr(main_2_output), .data({MicroOp, rom_1_data_2, or_1_out[0], rom_1_data}));  // open: sel

  // Notes on the sheet:
  //   SBR
endmodule
